// Logisim project hw1.circ as structural Verilog: 1 circuit, main circuit main
module main (
);

  wire and_1_out, and_2_out, and_3_out, and_4_out, and_5_out, and_6_out, and_7_out, and_8_out, and_9_out,
       and_10_out, and_11_out, and_12_out, and_13_out, and_14_out, and_15_out, and_16_out, and_17_out,
       and_18_out, and_19_out, and_20_out, button_1_out, button_2_out, button_3_out, button_4_out,
       button_5_out, button_6_out, d_ff_1_q, d_ff_1_qn, d_ff_2_q, d_ff_2_qn, d_ff_3_q, d_ff_3_qn, d_ff_4_q,
       d_ff_4_qn, d_ff_5_q, d_ff_5_qn, d_ff_6_q, d_ff_6_qn, nor_1_out, not_1_out, not_2_out, not_3_out,
       not_4_out, not_5_out, not_6_out, not_7_out, not_8_out, not_9_out, not_10_out, not_11_out, not_12_out,
       not_13_out, not_14_out, or_1_out, or_2_out, or_3_out, or_4_out, or_5_out, or_6_out, or_7_out,
       or_8_out, xor_1_out, xor_2_out, xor_3_out, xor_4_out;

  Button button_1 (.out(button_1_out));
  Button button_2 (.out(button_2_out));
  LED led_1 (.in(d_ff_2_q));
  D_Flip_Flop d_ff_1 (
    .clk(button_1_out), .D(d_ff_1_qn), .Q(d_ff_1_q), .Qn(d_ff_1_qn), .en(button_1_out));  // open: preset, reset
  D_Flip_Flop d_ff_2 (
    .clk(button_3_out), .D(d_ff_2_qn), .Q(d_ff_2_q), .Qn(d_ff_2_qn), .en(button_3_out));  // open: preset, reset
  LED led_2 (.in(d_ff_1_q));
  Button button_3 (.out(button_3_out));
  LED led_3 (.in(d_ff_3_q));
  D_Flip_Flop d_ff_3 (
    .clk(button_4_out), .D(d_ff_3_qn), .Q(d_ff_3_q), .Qn(d_ff_3_qn), .en(button_4_out));  // open: preset, reset
  LED led_4 (.in(d_ff_4_q));
  D_Flip_Flop d_ff_4 (
    .clk(button_2_out), .D(d_ff_4_qn), .Q(d_ff_4_q), .Qn(d_ff_4_qn), .en(button_2_out));  // open: preset, reset
  Button button_4 (.out(button_4_out));
  not not_1 (not_1_out, d_ff_1_q);
  not not_2 (not_2_out, d_ff_2_q);
  LED led_5 (.in(d_ff_5_q));
  D_Flip_Flop d_ff_5 (
    .clk(button_5_out), .D(d_ff_5_qn), .Q(d_ff_5_q), .Qn(d_ff_5_qn), .en(button_5_out));  // open: preset, reset
  Button button_5 (.out(button_5_out));
  xor xor_1 (xor_1_out, d_ff_2_q, d_ff_3_q);
  not not_3 (not_3_out, xor_1_out);
  not not_4 (not_4_out, xor_2_out);
  xor xor_2 (xor_2_out, d_ff_1_q, d_ff_4_q);
  or or_1 (or_1_out, not_1_out, d_ff_4_q);
  xor xor_3 (xor_3_out, d_ff_1_q, d_ff_4_q);
  or or_2 (or_2_out, not_2_out, d_ff_3_q);
  xor xor_4 (xor_4_out, d_ff_2_q, d_ff_3_q);
  and and_1 (and_1_out, d_ff_2_q, d_ff_3_q);
  and and_2 (and_2_out, d_ff_1_q, d_ff_4_q);
  or or_3 (or_3_out, d_ff_2_q, d_ff_3_q);
  or or_4 (or_4_out, d_ff_1_q, d_ff_4_q);
  not not_5 (not_5_out, d_ff_2_q);
  not not_6 (not_6_out, d_ff_1_q);
  LED led_6 (.in(d_ff_6_q));
  D_Flip_Flop d_ff_6 (
    .clk(button_6_out), .D(d_ff_6_qn), .Q(d_ff_6_q), .Qn(d_ff_6_qn), .en(button_6_out));  // open: preset, reset
  Button button_6 (.out(button_6_out));
  and and_3 (and_3_out, or_1_out, xor_3_out);
  not not_7 (not_7_out, and_3_out);
  and and_4 (and_4_out, or_2_out, xor_4_out);
  not not_8 (not_8_out, d_ff_5_q);
  and and_5 (and_5_out, not_8_out, d_ff_6_q);
  and and_6 (and_6_out, d_ff_5_q, not_9_out);
  not not_9 (not_9_out, d_ff_6_q);
  and and_7 (and_7_out, d_ff_5_q, d_ff_6_q);
  and and_8 (and_8_out, not_7_out, not_4_out, and_4_out);
  not not_10 (not_10_out, and_3_out);
  and and_9 (and_9_out, not_10_out, not_4_out, not_11_out);
  not not_11 (not_11_out, and_4_out);
  not not_12 (not_12_out, and_3_out);
  and and_10 (and_10_out, not_12_out, not_13_out);
  not not_13 (not_13_out, not_4_out);
  nor nor_1 (nor_1_out, d_ff_5_q, d_ff_6_q);
  or or_5 (or_5_out, and_3_out, and_8_out);
  not not_14 (not_14_out, not_3_out);
  and and_11 (and_11_out, not_14_out, and_9_out);
  or or_6 (or_6_out, and_11_out, and_10_out);
  and and_12 (and_12_out, not_3_out, not_4_out);
  and and_13 (and_13_out, or_5_out, nor_1_out);
  and and_14 (and_14_out, and_2_out, and_5_out);
  and and_15 (and_15_out, or_4_out, and_6_out);
  and and_16 (and_16_out, not_6_out, and_7_out);
  and and_17 (and_17_out, or_6_out, nor_1_out);
  and and_18 (and_18_out, and_1_out, and_5_out);
  and and_19 (and_19_out, or_3_out, and_6_out);
  and and_20 (and_20_out, not_5_out, and_7_out);
  // NOT_Gate not_15 is placed but not wired
  LED led_7 (.in(or_7_out));
  LED led_8 (.in(or_8_out));
  or or_7 (or_7_out, and_13_out, and_14_out, and_15_out, and_16_out);
  or or_8 (or_8_out, and_17_out, and_18_out, and_19_out, and_20_out);
  // AND_Gate and_21 is placed but not wired
  // OR_Gate or_9 is placed but not wired
  LED led_9 (.in(and_12_out));
  // XOR_Gate xor_5 is placed but not wired

  // Notes on the sheet:
  //   Data A 1
  //   Data B 1
  //   (1, 0) --> OR(A, B)
  //   (1, 1) --> NOT(A)
  //   A
  //   0
  //   Data A 0
  //   Data B 0
  //   (Instr 1, Instr 0) --> OP
  //   (0, 0) --> CMP(A, B)
  //   (0, 1) --> AND(A, B)
  //   B
  //   B
  //   A
  //   1
  //   0
  //   1
  //   A0 == B0
  //   A1 == B1
  //   Instr 1
  //   1
  //   0
  //   0
  //   1
  //   0
  //   1
  //   0
  //   1
  //   Instr 0
  //   VARIANT 2:
  //   B > A
  //   A > B
  //   B greater
  //   A == B
  //   A > B
  //   A < B
  //   A greater
  //   Out 1
  //   Out 0
  //   Build 4-uop 2-bit ALU
  //   Input and Output are presented
  //   Instruction set is described below
  //   You can use only the following elements (1-bit):
  //   CMP(A, B) truth table:
  //   "B greater"  "A greater"  "Equal"
  //   0                0                1
  //   0                1                0
  //   1                0                0
  //   Equal
endmodule
