// Logisim project test_hw1.circ as structural Verilog: 1 circuit, main circuit main
module main (
);

  wire and_1_out, and_2_out, and_3_out, and_5_out, nor_1_out, not_1_out, not_2_out;
  wire [1:0] and_4_out, and_6_out, and_7_out, and_8_out, and_9_out, bit_extender_1_out, bit_extender_2_out,
       bit_extender_3_out, bit_extender_4_out, not_3_out, or_1_out, or_2_out, xnor_1_out, xnor_2_out;

  LED led_1 (.in(and_5_out));
  LED led_2 (.in(or_2_out[1]));
  LED led_3 (.in(or_2_out[0]));
  not not_1 (not_1_out, 1'b1);
  not not_2 (not_2_out, 1'b1);
  assign xnor_1_out = ~(2'b10 ^ 2'b00);  // XNOR_Gate xnor_1, 2 bits wide
  nor nor_1 (nor_1_out, 1'b1, 1'b1);
  and and_1 (and_1_out, not_1_out, 1'b1);
  and and_2 (and_2_out, 1'b1, not_2_out);
  and and_3 (and_3_out, 1'b1, 1'b1);
  assign and_4_out = 2'b10 & 2'b00;  // AND_Gate and_4, 2 bits wide
  assign not_3_out = ~2'b10;  // NOT_Gate not_3, 2 bits wide
  assign xnor_2_out = ~(2'b10 ^ 2'b00);  // XNOR_Gate xnor_2, 2 bits wide
  assign or_1_out = 2'b10 | 2'b00;  // OR_Gate or_1, 2 bits wide
  and and_5 (and_5_out, xnor_1_out[0], xnor_1_out[1]);
  assign bit_extender_1_out = {{1{nor_1_out}}, nor_1_out};  // Bit_Extender bit_extender_1
  assign bit_extender_2_out = {{1{and_1_out}}, and_1_out};  // Bit_Extender bit_extender_2
  assign bit_extender_3_out = {{1{and_2_out}}, and_2_out};  // Bit_Extender bit_extender_3
  assign bit_extender_4_out = {{1{and_3_out}}, and_3_out};  // Bit_Extender bit_extender_4
  assign and_6_out = xnor_2_out & bit_extender_1_out;  // AND_Gate and_6, 2 bits wide
  assign and_7_out = and_4_out & bit_extender_2_out;  // AND_Gate and_7, 2 bits wide
  assign and_8_out = or_1_out & bit_extender_3_out;  // AND_Gate and_8, 2 bits wide
  assign and_9_out = not_3_out & bit_extender_4_out;  // AND_Gate and_9, 2 bits wide
  assign or_2_out = and_6_out | and_7_out | and_8_out | and_9_out;  // OR_Gate or_2, 2 bits wide

  // Notes on the sheet:
  //   A
  //   B
  //   opcode
  //   equal
  //   res
  //   opcodes:
  //   00 - CMP A B
  //   01 - AND A B
  //   10 - OR A B
  //   11 - NOT A
  //   A
  //   B
endmodule
